# Fritzing sketch circuit (saved by Fritzing 0.9.10b)
breadboards: 1

parts:
  Raspberry_Pi_1 = Raspberry Pi 3 [part_number=RPI-3-V1.2]
  LED2 = LED - 5mm [color="Yellow (585nm)" current=30mA package="5 mm [THT]"]
  R2 = Resistor [tolerance=±5% power=0.25 resistance=330 package=THT]
  LED4 = LED - 5mm [color="Green (555nm)" current=30mA package="5 mm [THT]"]
  R3 = Resistor [tolerance=±5% power=0.25 resistance=330 package=THT]
  LED5 = LED - 5mm [color="Blue (470nm)" current=30mA package="5 mm [THT]"]
  R4 = Resistor [tolerance=±5% power=0.25 resistance=330 package=THT]
  R1 = Resistor [tolerance=±5% power=0.25 resistance=330 package=THT]
  LED3 = LED - 5mm [color="Red (633nm)" current=30mA package="5 mm [THT]"]
  J1 = Piezo Speaker
  S1 = Pushbutton [package="[THT]"]
  S2 = Pushbutton [package="[THT]"]
  S3 = Pushbutton [package="[THT]"]
  S4 = Pushbutton [package="[THT]"]

nets:
  N1: Raspberry_Pi_1.GPIO2, S4.Pin_1, S4.Pin_2
  N2: Raspberry_Pi_1.GPIO3, S3.Pin_1, S3.Pin_2
  N3: Raspberry_Pi_1.GPIO4, S2.Pin_1, S2.Pin_2
  N4: Raspberry_Pi_1.GPIO17, S1.Pin_1, S1.Pin_2
  N5: Raspberry_Pi_1.GPIO5, J1.pin1
  N6: Raspberry_Pi_1.GND, LED2.cathode, LED4.cathode, LED5.cathode, LED3.cathode, J1.pin2, S1.Pin_3, S1.Pin_4, S2.Pin_3, S2.Pin_4, S3.Pin_3, S3.Pin_4, S4.Pin_3, S4.Pin_4
  N7: Raspberry_Pi_1.GPIO25, R1.Pin_0
  N8: Raspberry_Pi_1.GPIO24, R2.Pin_0
  N9: Raspberry_Pi_1.GPIO23, R3.Pin_0
  N10: Raspberry_Pi_1.GPIO18, R4.Pin_0
  N11: LED2.anode, R2.Pin_1
  N12: LED4.anode, R3.Pin_1
  N13: LED5.anode, R4.Pin_1
  N14: R1.Pin_1, LED3.anode

notes:
  GPIO18
  GPIO23
  GPIO24
  GPIO25
  GPIO5
  GPIO17
  GPIO4
  GPIO3
  GPIO2
